# Fritzing sketch sketch (saved by Fritzing 0.9.6b)
breadboards: 1

parts:
  "Wifi"_Arduino = Arduino Uno WIFI REV2
  "UX"_Arduino = Arduino Uno (Rev3) - ICSP
  RA8875 = Adafruit RA8875 Driver Board for 40-pin TFT Touch Displays [part_number="Adafruit #1590"]
  R1 = Resistor [tolerance=±5% power=0.25 resistance=220 package=THT]
  LED1 = LED - 5mm [color="Red (633nm)" current=0.030 package="5 mm [THT]"]
  R2 = Resistor [tolerance=±5% power=0.25 resistance=10k package=THT]
  BC550 = NPN-Transistor [package="TO92 [THT]"]
  R3 = Resistor [tolerance=±5% power=0.25 resistance=220 package=THT]
  R4 = Resistor [tolerance=±5% power=0.25 resistance=10k package=THT]
  C1 = Electrolytic Capacitor [capacitance=0.1mF voltage=35V package="100 mil [THT, electrolytic]"]
  D1 = Rectifier Diode [part_number=1N4001 package="300 mil [THT]"]
  R5 = Resistor [tolerance=±5% power=0.25 resistance=220 package=THT]
  LED2 = LED - 5mm [color="Red (633nm)" current=0.030 package="5 mm [THT]"]
  R6 = Resistor [tolerance=±5% power=0.25 resistance=10k package=THT]
  BC550_2 = NPN-Transistor [package="TO92 [THT]"]
  R7 = Resistor [tolerance=±5% power=0.25 resistance=220 package=THT]
  R8 = Resistor [tolerance=±5% power=0.25 resistance=10k package=THT]
  C2 = Electrolytic Capacitor [capacitance=0.1mF voltage=35V package="100 mil [THT, electrolytic]"]
  D2 = Rectifier Diode [part_number=1N4001 package="300 mil [THT]"]
  S3 = Toggle Switch [package=THT]
  S1 = Toggle Switch [package=THT]
  HW5P-1 = LTR-301 [package=ltr-301]
  R9 = Resistor [tolerance=±5% power=0.25 resistance=100k package=THT]
  S2 = Toggle Switch [package=THT]

nets:
  N1: "Wifi"_Arduino.RESET, D2.anode
  N2: "Wifi"_Arduino.5V, R8.Pin_1, C2.+
  GND: "Wifi"_Arduino.GND, "UX"_Arduino.GND, RA8875.GND, LED1.cathode, BC550.E, LED2.cathode, BC550_2.E, S3.L2, S1.L2, R9.Pin_0
  N3: "Wifi"_Arduino.D0/RX, "UX"_Arduino.D1/TX
  N4: "Wifi"_Arduino.D1/TX, S2.COM
  N5: "Wifi"_Arduino.D2, "UX"_Arduino.D2
  N6: "Wifi"_Arduino.D3_PWM, "UX"_Arduino.D3_PWM
  N7: "Wifi"_Arduino.D5_PWM, S1.COM
  N8: "Wifi"_Arduino.D7, R1.Pin_0, R2.Pin_0
  N9: "UX"_Arduino.A5/SCL, HW5P-1.E, R9.Pin_1
  5V: "UX"_Arduino.5V, RA8875.VIN, R4.Pin_1, C1.+, HW5P-1.C
  N10: "UX"_Arduino.RESET, D1.anode
  N11: "UX"_Arduino.D9_PWM, RA8875.RESET
  N12: "UX"_Arduino.D10_PWM/SS, RA8875.CS
  N13: "UX"_Arduino.D11_PWM/MOSI, RA8875.MOSI
  N14: "UX"_Arduino.D12/MISO, RA8875.MISO
  N15: "UX"_Arduino.D13/SCK, RA8875.SCK
  N16: "UX"_Arduino.D0/RX, S2.L1
  N17: "UX"_Arduino.D5_PWM, S3.COM
  N18: "UX"_Arduino.D7, R5.Pin_0, R6.Pin_0
  N19: R1.Pin_1, LED1.anode
  N20: R2.Pin_1, BC550.B
  N21: BC550.C, R3.Pin_0
  N22: R3.Pin_1, R4.Pin_0, C1.-, D1.cathode
  N23: R5.Pin_1, LED2.anode
  N24: R6.Pin_1, BC550_2.B
  N25: BC550_2.C, R7.Pin_0
  N26: R7.Pin_1, R8.Pin_0, C2.-, D2.cathode

notes:
  Close S1 on station 0 only
  Open S2 to upgrade software on UX Arduino
  Close S3 to force touchscreen re-calibration at boot

custom parts:
  Arduino Uno WIFI REV2: The Arduino Uno WIFI REV2 is a microcontroller board based on the ATmega 4809. It has 14 digital input/output pins (of which 5 can be used as PWM outputs), 6 analog inputs, a 16 MHz ceramic resonator, a USB connection, a power jack, an ICSP header, and a reset button. It also has a WIFI controller with a secure ECC608 crypto unit and an internal IMU. It contains everything needed to support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
  Adafruit RA8875 Driver Board for 40-pin TFT Touch Displays: Have you gazed longingly at large TFT displays - you know what I'm talking about here, 4", 5" or 7" TFTs with up to 800x480 pixels. Then you look at your Arduino. You love your Arduino (you really do!) but there's no way it can control a display like that, one that requires 60Hz refresh and 4 MHz pixel clocking. Heck, it doesn't even have enough pins. I suppose you could move to ARM core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
